# Fritzing sketch phone_controlled_car (saved by Fritzing 0.8.7b)
breadboards: 1

parts:
  U1 = NodeMCU V1.0
  S1 = H-Bridge with L298N
  M1 = DC Motor
  M2 = DC Motor
  U2 = LIPO-2000mAh [package=lipo-2000]

nets:
  N1: U1.D3, U1.D4, S1.IN1, S1.IN2
  GND: U1.GND, S1.GND, U2.-
  N2: U1.D5, S1.ENB
  N3: U1.D6, S1.ENA
  N4: U1.D7, S1.IN3
  N5: U1.D8, S1.IN4
  VIN: U1.Vin, S1.12V, U2.+
  N6: S1.M1-01, M1.pin_2
  N7: S1.M1-02, M1.pin_1
  N8: S1.M2-01, M2.pin_2
  N9: S1.M2-02, M2.pin_1

custom parts:
  NodeMCU V1.0: ESP8266 based NodeMCU
  H-Bridge with L298N: h-bridge
